# Fritzing sketch arduino-esp8266-connected (saved by Fritzing 0.9.2b)
breadboards: 1

parts:
  part = ESP8266 ESP01 [part_number=ESP8266 package=THT]
  LM1117-3_3V = V_REG_LD1117VXX [package=78xxl]
  C1 = Electrolytic Capacitor [capacitance=10µF package="100 mil [THT, electrolytic]"]
  C2 = Electrolytic Capacitor [capacitance=22µF package="100 mil [THT, electrolytic]"]
  부품1 = Arduino Uno (Rev3)
  R1 = Resistor [tolerance=±5% resistance=1k package=THT]
  R2 = Resistor [tolerance=±5% resistance=2.2k package=THT]
  R3 = Resistor [tolerance=±5% resistance=10k package=THT]
  S2 = Pushbutton [package="[THT]"]
  R5 = Resistor [tolerance=±5% resistance=1k package=THT]
  S3 = Toggle Switch [package=THT]
  R6 = Resistor [tolerance=±5% resistance=330 package=THT]
  LED1 = LED - 5mm [color="Red (633nm)" package="5 mm [THT]"]

nets:
  GND: part.GND, LM1117-3_3V.GND, C1.-, C2.-, 부품1.GND, R2.Pin_0, S2.Pin_3, S2.Pin_4, S3.L2, R6.Pin_1
  N1: part.RXD, R1.Pin_1, R2.Pin_1
  N2: part.TXD, 부품1.D2
  N3: part.VCC, LM1117-3_3V.OUT, C2.+, R3.Pin_1, R5.Pin_1
  N4: part.GPIO16, S2.Pin_1, S2.Pin_2, R5.Pin_0
  N5: part.GPIO00, S3.COM
  N6: part.GPIO02, LED1.anode
  N7: part.CH_PD, R3.Pin_0
  N8: LM1117-3_3V.IN, C1.+, 부품1.5V
  N9: 부품1.D3_PWM, R1.Pin_0
  N10: R6.Pin_0, LED1.cathode

custom parts:
  ESP8266 ESP01: Generic WiFi Module based on the ESP8266 with onboard PCB antenna and UART communications
