# Fritzing sketch arduino-firmata (saved by Fritzing 0.9.2b)
breadboards: 1

parts:
  S1 = Pushbutton [package="[THT]"]
  R1 = Resistor [tolerance=±5% resistance=330 package=THT]
  부품1 = Arduino Uno (Rev3)
  LED1 = LED - 5mm [color="Red (633nm)" package="5 mm [THT]"]
  R4 = Resistor [tolerance=±5% resistance=10k package=THT]

nets:
  N1: S1.Pin_1, S1.Pin_2, 부품1.5V
  N2: S1.Pin_3, S1.Pin_4, 부품1.D4, R4.Pin_1
  N3: R1.Pin_0, 부품1.D5_PWM
  N4: R1.Pin_1, LED1.anode
  N5: 부품1.GND, LED1.cathode, R4.Pin_0
