# Fritzing sketch arduino-greenhouse (saved by Fritzing 0.9.2b)
breadboards: 2

parts:
  부품1 = Arduino Uno (Rev3)
  U2 = ESP8266 WiFi Module [part_number=ESP8266]
  R5 = Resistor [tolerance=±5% resistance=10k package=THT]
  L293D1 = IC, DIP package, 16 pins [chip_label=L293D]
  R6 = PHOTOCELL [package=photocell-kit]
  NEOPIXEL1 = Neopixel Strip -- White (60/m)
  Power_plug1 = Power plug
  R7 = Resistor [tolerance=±5% resistance=10k package=THT]
  S4 = Pushbutton [package="[THT]"]
  R8 = Resistor [tolerance=±5% resistance=1k package=THT]
  S5 = Toggle Switch [package=THT]
  LED2 = LED - 5mm [color="Red (633nm)" package="5 mm [THT]"]
  R9 = Resistor [tolerance=±5% resistance=10k package=THT]
  R10 = Resistor [tolerance=±5% resistance=1k package=THT]
  R11 = Resistor [tolerance=±5% resistance=330 package=THT]
  R12 = Resistor [tolerance=±5% resistance=2.2k package=THT]
  LM1117-3_3V1 = V_REG_LD1117VXX [package=78xxl]
  C3 = Electrolytic Capacitor [capacitance=10µF package="100 mil [THT, electrolytic]"]
  C4 = Electrolytic Capacitor [capacitance=22µF package="100 mil [THT, electrolytic]"]
  DHT4 = DHT22 Humidity and Temperature Sensor

nets:
  N1: 부품1.A0, R6.P$1, R7.Pin_0
  N2: 부품1.D8, L293D1.pin2
  N3: 부품1.D9_PWM, L293D1.pin1
  GND: 부품1.GND, U2.GND, L293D1.pin4, L293D1.pin5, L293D1.pin12, L293D1.pin13, NEOPIXEL1.GND, Power_plug1.GND, R7.Pin_1, S4.Pin_3, S4.Pin_4, S5.L2, R11.Pin_1, R12.Pin_0, LM1117-3_3V1.GND, C3.-, C4.-, DHT4.GND
  N4: 부품1.D2, U2.TXD
  N5: 부품1.D3_PWM, R10.Pin_0
  N6: 부품1.D4, R5.Pin_0, DHT4.DATA
  N7: 부품1.D5_PWM, L293D1.pin9
  N8: 부품1.D6_PWM, L293D1.pin10
  5V: 부품1.5V, R5.Pin_1, L293D1.pin3, L293D1.pin16, R6.P$2, NEOPIXEL1.+5V, LM1117-3_3V1.IN, C3.+, DHT4.VDD
  N9: U2.RXD, R10.Pin_1, R12.Pin_1
  N10: U2.VCC, R8.Pin_1, R9.Pin_1, LM1117-3_3V1.OUT, C4.+
  N11: U2.GPIO_0, S5.COM
  N12: U2.GPIO_16, S4.Pin_1, S4.Pin_2, R8.Pin_0
  N13: U2.GPIO_2, LED2.anode
  N14: U2.CH_PD, R9.Pin_0
  N15: L293D1.pin8, Power_plug1.VCC
  N16: LED2.cathode, R11.Pin_0

custom parts:
  ESP8266 WiFi Module: Generic WiFi Module based on the ESP8266 with onboard PCB antenna and UART communications
  Neopixel Strip -- White (60/m): Neopixel Strip, White, 60 pixels per meter.
