# Fritzing sketch arduino-hm10 (saved by Fritzing 0.9.1b)
breadboards: 1

parts:
  부품1 = BLE HM-10 Breakout
  아두이노 = Arduino Uno (Rev3)

nets:
  N1: 부품1.TXD, 아두이노.D2
  N2: 부품1.RXD, 아두이노.D3_PWM
  VCC: 부품1.VCC, 아두이노.3V3
  GND: 부품1.GND, 아두이노.GND
