# Fritzing sketch arduino-serial (saved by Fritzing 0.9.2b)
breadboards: 1

parts:
  부품1 = Arduino Uno (Rev3)
  Raspberry_Pi1 = Raspberry Pi 2
  R1 = Resistor [tolerance=±5% resistance=1k package=THT]
  R2 = Resistor [tolerance=±5% resistance=1k package=THT]
  R3 = Resistor [tolerance=±5% resistance=1k package=THT]

nets:
  GND: 부품1.GND, Raspberry_Pi1.GND, R2.Pin_1
  N1: 부품1.D0/RX, Raspberry_Pi1.GPIO14
  N2: 부품1.D1/TX, R1.Pin_1, R3.Pin_1
  5V: 부품1.5V, Raspberry_Pi1.5V
  N3: Raspberry_Pi1.GPIO15, R1.Pin_0, R2.Pin_0, R3.Pin_0
