# Fritzing sketch arduino-xbee (saved by Fritzing 0.9.2b)

parts:
  부품2 = Arduino Uno (Rev3)
  부품3 = Arduino Wireless SD Shield

nets:
  N1: 부품2.A0, 부품3.A0
  N2: 부품2.A1, 부품3.A1
  N3: 부품2.A2, 부품3.A2
  N4: 부품2.A3, 부품3.A3
  N5: 부품2.A4/SDA, 부품3.A4
  N6: 부품2.A5/SCL, 부품3.A5
  N7: 부품2.D8, 부품3.D8
  N8: 부품2.D9_PWM, 부품3.D9
  N9: 부품2.D10_PWM/SS, 부품3.D10
  N10: 부품2.D11_PWM/MOSI, 부품3.D11
  N11: 부품2.D12/MISO, 부품3.D12
  N12: 부품2.D13/SCK, 부품3.D13
  GND: 부품2.GND, 부품3.GND
  N13: 부품2.AREF, 부품3.AREF
  N14: 부품2.D0/RX, 부품3.ARDUINO-RX(0)
  N15: 부품2.D1/TX, 부품3.ARDUINO-TX(1)
  N16: 부품2.D2, 부품3.D2
  N17: 부품2.D3_PWM, 부품3.D3
  N18: 부품2.D4, 부품3.SD_CS
  N19: 부품2.D5_PWM, 부품3.D5
  N20: 부품2.D6_PWM, 부품3.D6
  N21: 부품2.D7, 부품3.D7
  N22: 부품2.RESET, 부품3.RESET
  3V3: 부품2.3V3, 부품3.3.3V
  5V: 부품2.5V, 부품3.+5V
  VIN: 부품2.VIN, 부품3.VIN
