# Fritzing sketch nodemcu-leddht22 (saved by Fritzing 0.9.2b)
breadboards: 1

parts:
  U1 = Nodemcu Breakout [part_number=nodemcu]
  DHT22 = DHT22 Humidity and Temperature Sensor
  LED1 = LED - 5mm [color="Red (633nm)" package="5 mm [THT]"]
  R2 = Resistor [tolerance=±5% resistance=330 package=THT]
  R3 = Resistor [tolerance=±5% resistance=10k package=THT]

nets:
  GND: U1.GND, DHT22.GND, R2.Pin_0
  3V3: U1.3V3, U1.3.3V, DHT22.VDD, R3.Pin_0
  N1: U1.D4, DHT22.DATA, R3.Pin_1
  N2: U1.D2, LED1.anode
  N3: LED1.cathode, R2.Pin_1

custom parts:
  Nodemcu Breakout: Nodemcu Breakout Board Based on ESP8266 ESP-12E module with onboard PCB antenna and USB/UART connector
