# Fritzing sketch particle-led (saved by Fritzing 0.9.1b)
breadboards: 1

parts:
  R2 = Resistor [tolerance=±5% resistance=330 package=THT]
  LED1 = smd LED [color="Red (633nm)" package="0603 [SMD]"]
  Spark_Core = Spark Core (v1.0)

nets:
  N1: R2.Pin_0, Spark_Core.D0
  N2: R2.Pin_1, LED1.anode
  N3: LED1.cathode, Spark_Core.GND
