# Fritzing sketch particle-led3 (saved by Fritzing 0.9.2b)
breadboards: 1

parts:
  LED1 = smd LED [color="Green (570nm)" package="0603 [SMD]"]
  Spark_Core = Spark Core (v1.0)
  LED2 = smd LED [color="Yellow (595nm)" package="0603 [SMD]"]
  LED3 = smd LED [color="Red (633nm)" package="0603 [SMD]"]
  R2 = Resistor [tolerance=±5% resistance=330 package=THT]
  R3 = Resistor [tolerance=±5% resistance=330 package=THT]
  R4 = Resistor [tolerance=±5% resistance=330 package=THT]

nets (from the breadboard view):
  N1: LED1.cathode, R2.Pin_1
  N2: LED1.anode, Spark_Core.D0
  N3: Spark_Core.GND, R2.Pin_0, R3.Pin_0, R4.Pin_0
  N4: Spark_Core.D1, LED2.anode
  N5: Spark_Core.D2, LED3.anode
  N6: LED2.cathode, R3.Pin_1
  N7: LED3.cathode, R4.Pin_1
