# Fritzing sketch particle-leddht22 (saved by Fritzing 0.9.2b)
breadboards: 1

parts:
  부품1 = Spark Core (v1.0)
  R2 = Resistor [tolerance=±5% resistance=10k package=THT]
  LED2 = smd LED [color="Red (633nm)" package="0603 [SMD]"]
  R3 = Resistor [tolerance=±5% resistance=330 package=THT]
  DHT2 = DHT22 Humidity and Temperature Sensor

nets:
  GND: 부품1.GND, R3.Pin_1, DHT2.GND
  N1: 부품1.D0, R2.Pin_0, DHT2.DATA
  N2: 부품1.D7, LED2.anode
  N3: 부품1.3V3*, R2.Pin_1, DHT2.VDD
  N4: LED2.cathode, R3.Pin_0
