# Fritzing sketch acc_lsm303dlhc_direct (saved by Fritzing 0.9.2b)

parts:
  LSM1 = LSM303DLHC Breakout
  Raspberry_Pi_B_rev1 = Raspberry Pi 2

nets:
  VCC: LSM1.VCC, Raspberry_Pi_B_rev1.3v3
  GND: LSM1.GND, Raspberry_Pi_B_rev1.GND
  N1: LSM1.SDA, Raspberry_Pi_B_rev1.GPIO2
  N2: LSM1.SCL, Raspberry_Pi_B_rev1.GPIO3

custom parts:
  LSM303DLHC Breakout: LSM303DLHC Accelrometer and Magnetometer Breakout Board
