# Fritzing sketch accgyro_direct (saved by Fritzing 0.9.2b)

parts:
  LSM1 = LSM303DLHC Breakout
  L3G4200D1 = L3G4200D Breakout
  Raspberry_Pi_B_rev1 = Raspberry Pi 2

nets:
  3V3: LSM1.VCC, LSM1.pin_10, L3G4200D1.VCC2, Raspberry_Pi_B_rev1.3v3, Raspberry_Pi_B_rev1.3V3
  GND: LSM1.GND, LSM1.pin_20, L3G4200D1.GND2, Raspberry_Pi_B_rev1.GND
  N1: LSM1.SDA, LSM1.pin_30, L3G4200D1.SDA, Raspberry_Pi_B_rev1.GPIO2, Raspberry_Pi_B_rev1.5V
  N2: LSM1.SCL, LSM1.pin_40, L3G4200D1.SCL, Raspberry_Pi_B_rev1.GPIO3

custom parts:
  LSM303DLHC Breakout: LSM303DLHC Accelrometer and Magnetometer Breakout Board
  L3G4200D Breakout: L3G4200D Gyroscope Sensor Breakout Board
