# Fritzing sketch adc_mcp3008 (saved by Fritzing 0.9.2b)
breadboards: 1

parts:
  IC2 = MCP3008 8-channel 10-bit ADC [part_number=MCP3008]
  R1 = Rotary Potentiometer (Small) [maximum_resistance=100kΩ package=THT]
  Raspberry_Pi_B_rev1 = Raspberry Pi 2

nets:
  N1: IC2.no_name_yet#1, R1.wiper
  N2: IC2.no_name_yet#9, IC2.no_name_yet#14, R1.leg1, Raspberry_Pi_B_rev1.GND
  N3: IC2.no_name_yet#10, Raspberry_Pi_B_rev1.GPIO8
  N4: IC2.no_name_yet#11, Raspberry_Pi_B_rev1.GPIO10
  N5: IC2.no_name_yet#12, Raspberry_Pi_B_rev1.GPIO9
  N6: IC2.no_name_yet#13, Raspberry_Pi_B_rev1.GPIO11
  3V3: IC2.no_name_yet#15, IC2.no_name_yet#16, R1.leg2, Raspberry_Pi_B_rev1.3v3, Raspberry_Pi_B_rev1.3V3
