# Fritzing sketch cp2102_direct (saved by Fritzing 0.9.2b)

parts:
  Raspberry_Pi = Raspberry Pi 2
  USBUART = CP2102 USB UART Breakout

nets:
  3V3: Raspberry_Pi.3v3, Raspberry_Pi.3V3, USBUART.VCCIO
  GND: Raspberry_Pi.GND, USBUART.GND
  N1: Raspberry_Pi.GPIO15, USBUART.TXD
  N2: Raspberry_Pi.GPIO14, USBUART.RXD

custom parts:
  CP2102 USB UART Breakout: CP2102 Usb Uart Breakout Board with Battery
