# Fritzing sketch dc_motor (saved by Fritzing 0.9.2b)
breadboards: 1

parts:
  Power_plug = Power plug
  M1 = DC Motor
  L293D = IC, DIP package, 16 pins [chip_label=L293D]
  VCC = 4 x AAA Battery Mount
  Raspberry_Pi_2 = Raspberry Pi 2

nets:
  N1: Power_plug.GND, L293D.pin12, VCC.+
  N2: Power_plug.VCC, L293D.pin8, VCC.-
  N3: M1.pin_1, L293D.pin6
  N4: M1.pin_2, L293D.pin3
  N5: L293D.pin1, Raspberry_Pi_2.GPIO18
  N6: L293D.pin2, Raspberry_Pi_2.GPIO23
  N7: L293D.pin5, Raspberry_Pi_2.GND
  N8: L293D.pin7, Raspberry_Pi_2.GPIO24
  N9: L293D.pin16, Raspberry_Pi_2.5V

custom parts:
  4 x AAA Battery Mount: A 4 x AAA battery pack (4.8 Volts with recharables)
