# Fritzing sketch df_at45dbxx (saved by Fritzing 0.9.2b)
breadboards: 1

parts:
  IC3 = IC, DIP package, 8 pins [chip_label=AT45DBXX]
  Raspberry_Pi_B_rev1 = Raspberry Pi 2

nets:
  N1: IC3.pin1, Raspberry_Pi_B_rev1.GPIO10
  N2: IC3.pin2, Raspberry_Pi_B_rev1.GPIO11
  N3: IC3.pin4, Raspberry_Pi_B_rev1.GPIO8
  N4: IC3.pin5, Raspberry_Pi_B_rev1.GPIO7
  N5: IC3.pin6, Raspberry_Pi_B_rev1.3v3
  N6: IC3.pin7, Raspberry_Pi_B_rev1.GND
  N7: IC3.pin8, Raspberry_Pi_B_rev1.GPIO9
