# Fritzing sketch df_at45dbxx_direct (saved by Fritzing 0.9.2b)

parts:
  DataFlash1 = AT45DBXX Dataflash Breakout
  Raspberry_Pi_B_rev1 = Raspberry Pi 2

nets:
  VCC: DataFlash1.VCC, Raspberry_Pi_B_rev1.3v3
  GND: DataFlash1.GND, Raspberry_Pi_B_rev1.GND
  N1: DataFlash1.MISO, Raspberry_Pi_B_rev1.GPIO10
  N2: DataFlash1.MOSI, Raspberry_Pi_B_rev1.GPIO9
  N3: DataFlash1.SCK, Raspberry_Pi_B_rev1.GPIO11
  N4: DataFlash1./CS, Raspberry_Pi_B_rev1.GPIO8
  N5: DataFlash1./WP, Raspberry_Pi_B_rev1.GPIO7

custom parts:
  AT45DBXX Dataflash Breakout: AT45DBXX DataFlash Breakout Board with Battery
