# Fritzing sketch gyro_l3g4200d_direct (saved by Fritzing 0.9.2b)

parts:
  L3G4200D1 = L3G4200D Breakout
  Raspberry_Pi_B_rev1 = Raspberry Pi 2

nets:
  VCC: L3G4200D1.VCC, L3G4200D1.VCC2, Raspberry_Pi_B_rev1.3v3
  GND: L3G4200D1.GND, L3G4200D1.GND2, Raspberry_Pi_B_rev1.GND
  N1: L3G4200D1.SDA, Raspberry_Pi_B_rev1.GPIO2
  N2: L3G4200D1.SCL, Raspberry_Pi_B_rev1.GPIO3

custom parts:
  L3G4200D Breakout: L3G4200D Gyroscope Sensor Breakout Board
