# Fritzing sketch lcd1602 (saved by Fritzing 0.9.2b)
breadboards: 1

parts:
  R1 = Rotary Potentiometer (Small) [maximum_resistance=100kΩ package=THT]
  LCD1 = LCD screen
  Raspberry_Pi_B_rev1 = Raspberry Pi 2

nets:
  VSS: R1.leg1, LCD1.VSS, LCD1.R/W, LCD1.LED-, Raspberry_Pi_B_rev1.GND
  N1: R1.wiper, LCD1.V0
  3V3: R1.leg2, LCD1.VDD, LCD1.LED+, Raspberry_Pi_B_rev1.3v3, Raspberry_Pi_B_rev1.3V3
  N2: LCD1.RS, Raspberry_Pi_B_rev1.GPIO22
  N3: LCD1.E, Raspberry_Pi_B_rev1.GPIO11
  N4: LCD1.DB4, Raspberry_Pi_B_rev1.GPIO23
  N5: LCD1.DB5, Raspberry_Pi_B_rev1.GPIO10
  N6: LCD1.DB6, Raspberry_Pi_B_rev1.GPIO9
  N7: LCD1.DB7, Raspberry_Pi_B_rev1.GPIO25
