# Fritzing sketch led3 (saved by Fritzing 0.9.1b)
breadboards: 1

parts:
  R2 = Resistor [tolerance=±5% resistance=330 package=THT]
  LED1 = smd LED [color="Red (633nm)" package="0603 [SMD]"]
  LED2 = smd LED [color="Yellow (595nm)" package="0603 [SMD]"]
  R3 = Resistor [tolerance=±5% resistance=330 package=THT]
  LED3 = smd LED [color="Green (570nm)" package="0603 [SMD]"]
  R4 = Resistor [tolerance=±5% resistance=330 package=THT]
  Raspberry_Pi_B_rev1 = Raspberry Pi B+

nets:
  N1: R2.Pin_0, Raspberry_Pi_B_rev1.GPIO18
  N2: R2.Pin_1, LED1.anode
  N3: LED1.cathode, LED2.cathode, LED3.cathode, Raspberry_Pi_B_rev1.GND
  N4: LED2.anode, R3.Pin_1
  N5: R3.Pin_0, Raspberry_Pi_B_rev1.GPIO23
  N6: LED3.anode, R4.Pin_1
  N7: R4.Pin_0, Raspberry_Pi_B_rev1.GPIO24
