# Fritzing sketch ledsw (saved by Fritzing 0.9.2b)
breadboards: 1

parts:
  S1 = Pushbutton [package="[THT]"]
  R1 = Resistor [tolerance=±5% resistance=330 package=THT]
  LED1 = LED - 5mm [color="Red (633nm)" package="5 mm [THT]"]
  R3 = Resistor [tolerance=±5% resistance=10k package=THT]
  LED2 = LED - 5mm [color="Red (633nm)" package="5 mm [THT]"]
  R2 = Resistor [tolerance=±5% resistance=330 package=THT]
  Raspberry_Pi_B_rev1 = Raspberry Pi 2

nets:
  3V3: S1.Pin_1, S1.Pin_2, Raspberry_Pi_B_rev1.3v3, Raspberry_Pi_B_rev1.3V3
  N1: S1.Pin_3, S1.Pin_4, R3.Pin_1, Raspberry_Pi_B_rev1.GPIO24
  N2: R1.Pin_0, Raspberry_Pi_B_rev1.GPIO18
  N3: R1.Pin_1, LED1.anode
  N4: LED1.cathode, R3.Pin_0, LED2.cathode, Raspberry_Pi_B_rev1.GND
  N5: LED2.anode, R2.Pin_1
  N6: R2.Pin_0, Raspberry_Pi_B_rev1.GPIO23
