# Fritzing sketch rpi_leddht22 (saved by Fritzing 0.9.2b)
breadboards: 1

parts:
  R1 = Resistor [tolerance=±5% resistance=10k package=THT]
  Raspberry_Pi_B_rev1 = Raspberry Pi 2
  DHT2 = DHT22 Humidity and Temperature Sensor
  LED1 = LED - 5mm [color="Red (633nm)" package="5 mm [THT]"]
  R2 = Resistor [tolerance=±5% resistance=330 package=THT]

nets:
  N1: R1.Pin_0, Raspberry_Pi_B_rev1.GPIO18, DHT2.DATA
  3V3: R1.Pin_1, Raspberry_Pi_B_rev1.3v3, Raspberry_Pi_B_rev1.3V3, DHT2.VDD
  N2: Raspberry_Pi_B_rev1.GPIO17, LED1.anode
  GND: Raspberry_Pi_B_rev1.GND, DHT2.GND, R2.Pin_0
  N3: LED1.cathode, R2.Pin_1
