# Fritzing sketch rtc_pcf8563 (saved by Fritzing 0.9.2b)
breadboards: 1

parts:
  BAT1 = Battery Holders [package=battcom_20mm_pth]
  C1 = Ceramic Capacitor [capacitance=10pF package="100 mil [THT, multilayer]"]
  Y3 = CRYSTAL [package=tc38h]
  PCF8563 = DS1307 [package=THT]
  Raspberry_Pi_B_rev1 = Raspberry Pi 2

nets:
  N1: BAT1.+, C1.0, PCF8563.+V
  N2: BAT1.-, C1.1, PCF8563.0V, Raspberry_Pi_B_rev1.GND
  N3: Y3.1, PCF8563.OSC1_-_Crystal
  N4: Y3.2, PCF8563.OSC0_-_Crystal
  N5: PCF8563.SDA_-_I2C_Data, Raspberry_Pi_B_rev1.GPIO2
  N6: PCF8563.SCL_-_I2C_Clock, Raspberry_Pi_B_rev1.GPIO3

custom parts:
  DS1307: DS1307 I2C Real Time Clock
