# Fritzing sketch servo_motor (saved by Fritzing 0.9.2b)
breadboards: 1

parts:
  J1 = Basic Servo
  R1 = Resistor [tolerance=±5% resistance=10k package=THT]
  Power_plug = Power plug
  VCC = 4 x AAA Battery Mount
  Raspberry_Pi_2 = Raspberry Pi 2

nets:
  GND: J1.gnd, Power_plug.GND, VCC.+, Raspberry_Pi_2.GND
  VCC: J1.vcc, Power_plug.VCC, VCC.-
  N1: J1.pulse, R1.Pin_1
  N2: R1.Pin_0, Raspberry_Pi_2.GPIO18

custom parts:
  4 x AAA Battery Mount: A 4 x AAA battery pack (4.8 Volts with recharables)
