# Fritzing sketch sw (saved by Fritzing 0.9.2b)
breadboards: 1

parts:
  S1 = Pushbutton [package="[THT]"]
  R1 = Resistor [tolerance=±5% resistance=10k package=THT]
  Raspberry_Pi_B_rev1 = Raspberry Pi 2

nets:
  N1: S1.Pin_1, S1.Pin_2, Raspberry_Pi_B_rev1.3v3
  N2: S1.Pin_3, S1.Pin_4, R1.Pin_1, Raspberry_Pi_B_rev1.GPIO24
  N3: R1.Pin_0, Raspberry_Pi_B_rev1.GND
