# Fritzing sketch sw2 (saved by Fritzing 0.9.2b)
breadboards: 1

parts:
  S1 = Pushbutton [package="[THT]"]
  R1 = Resistor [tolerance=±5% resistance=10k package=THT]
  R2 = Resistor [tolerance=±5% resistance=10k package=THT]
  S2 = Pushbutton [package="[THT]"]
  Raspberry_Pi_B_rev1 = Raspberry Pi 2

nets:
  3V3: S1.Pin_1, S1.Pin_2, R2.Pin_0, Raspberry_Pi_B_rev1.3v3, Raspberry_Pi_B_rev1.3V3
  N1: S1.Pin_3, S1.Pin_4, R1.Pin_1, Raspberry_Pi_B_rev1.GPIO24
  N2: R1.Pin_0, S2.Pin_1, S2.Pin_2, Raspberry_Pi_B_rev1.GND
  N3: R2.Pin_1, S2.Pin_3, S2.Pin_4, Raspberry_Pi_B_rev1.GPIO23
