# Fritzing sketch temp_ds18b20 (saved by Fritzing 0.9.2b)
breadboards: 1

parts:
  DS1 = DS18B20 1-Wire Temperature Sensor [part_number=DS18B20]
  R1 = Resistor [tolerance=±5% resistance=10k package=THT]
  Raspberry_Pi_B_rev1 = Raspberry Pi 2

nets:
  VDD: DS1.VDD, R1.Pin_1, Raspberry_Pi_B_rev1.3v3
  N1: DS1.DQ, R1.Pin_0, Raspberry_Pi_B_rev1.GPIO4
  GND: DS1.GND, Raspberry_Pi_B_rev1.GND
