# Fritzing sketch xbee (saved by Fritzing 0.9.2b)
breadboards: 1

parts:
  Raspberry_Pi = Raspberry Pi 2
  U1 = XBEE-1 [package=xbee-1]

nets:
  3V3: Raspberry_Pi.3v3, U1.VDD
  N1: Raspberry_Pi.GPIO15, U1.DOUT
  N2: Raspberry_Pi.GPIO14, U1.DIN
  GND: Raspberry_Pi.GND, U1.GND
